# Fritzing sketch Jetson_Arduino (saved by Fritzing 0.9.10b)

parts:
  Jetson_Nano2 = jetsonnano
  Composant1 = Arduino Uno (Rev3)
  J1 = Basic Servo

nets:
  N1: Jetson_Nano2.connector6, Composant1.A5/SCL
  GND: Jetson_Nano2.connector32, Composant1.GND, J1.gnd
  N2: Jetson_Nano2.connector33, Composant1.A4/SDA
  N3: Composant1.D2, J1.pulse
  5V: Composant1.5V, J1.vcc
